# Fritzing sketch XMAS Lights (saved by Fritzing 0.9.3b)
breadboards: 1

parts:
  U1 = NodeMCU V1.0
  Part1 = Logic Level Converter
  5V = DC Power [voltage=5]
  NEOPIXEL1 = Neopixel Strip -- White (30/m) [part_number=1376]
  C1 = Capacitor Polarized [package=panasonic_h13]
  JP1 = USB_MICROB_PLUG [package=micro-b-th]

nets:
  N1: U1.3V3, Part1.LV
  GND: U1.GND, C1.-
  N2: U1.TX, Part1.TX_LV
  N3: Part1.TX_HV, NEOPIXEL1.Din
  +5V: Part1.HV, 5V.V+, NEOPIXEL1.+5V, C1.+, JP1.VCC

custom parts:
  NodeMCU V1.0: ESP8266 based NodeMCU
  Neopixel Strip -- White (30/m): These NeoPixel strips have 30 digitally-addressable pixel LEDs per meter and are very affordable and are only 12.5 mm wide, 10 mm if you remove the strip from the casing.
